# Fritzing sketch Wiring (saved by Fritzing 0.9.3b)
breadboards: 1

parts:
  Part1 = NeoPixel Stick [part_number=1426]
  Part2 = Arduino Nano (Rev3.0)
  Power_plug1 = Power plug

nets:
  GND: Part1.GND, Part2.GND, Power_plug1.GND
  +5V: Part1.+5V, Part2.VIN, Power_plug1.VCC

custom parts:
  NeoPixel Stick: Make your own little LED strip arrangement with this stick of NeoPixel LEDs. We crammed 8 of the tiny 5050 (5mm x 5mm) smart RGB LEDs onto a PCB with mounting holes and a chainable design. Use only one microcontroller pin to control as many as you can chain together! Each LED is addressable as the driver chip is inside the LED. Each one has ~18mA constant current drive so the color will be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
